# Fritzing sketch LED_board_1 (saved by Fritzing 0.9.3b)
breadboards: 1

parts:
  R1 = Resistor [tolerance=±5% resistance=220 package=THT]
  R2 = Resistor [tolerance=±5% resistance=2.2k package=THT]
  LED3 = LED - 3mm [color="White (4500K)" package="3 mm [THT]"]
  LED1 = LED - 3mm [color="White (4500K)" package="3 mm [THT]"]
  LED2 = LED - 3mm [color="White (4500K)" package="3 mm [THT]"]
  Q1 = NPN-Transistor [package="TO92 [THT]"]

nets:
  N1: R1.Pin_0, LED3.anode, LED1.anode, LED2.anode
  5V: R1.Pin_1
  N2: R2.Pin_0, Q1.B
  Din: R2.Pin_1
  N3: LED3.cathode, LED1.cathode, LED2.cathode, Q1.C
  GND: Q1.E

notes:
  Forest Park Wall Board, Low-current LED array switch using NPN transistor.  Active high enable., 1
