# Fritzing sketch LED_board_2 (saved by Fritzing 0.9.3b)
breadboards: 1

parts:
  R1 = Resistor [tolerance=±5% resistance=470 package=THT]
  R2 = Resistor [tolerance=±5% resistance=2.2k package=THT]
  LED3 = LED - 3mm [color="Red (635nm)" package="3 mm [THT]"]
  LED1 = LED - 3mm [color="Red (635nm)" package="3 mm [THT]"]
  LED2 = LED - 3mm [color="Red (635nm)" package="3 mm [THT]"]
  Q1 = PNP-Transistor [package="TO92 [THT]"]

nets:
  N1: R1.Pin_0, LED3.anode, LED1.anode, LED2.anode
  5V: R1.Pin_1
  N2: R2.Pin_0, Q1.B
  Din: R2.Pin_1
  N3: LED3.cathode, LED1.cathode, LED2.cathode, Q1.E
  GND: Q1.C

notes:
  Forest Park Wall Board, Low-current LED array switch using PNP transistor.  Active low enable., 1
